// Logisim project alu.circ as structural Verilog: 2 circuits, main circuit main
module main (
  input  [1:0] in_1,
  input  in_2,
  input  [3:0] in_3,
  input  [3:0] in_4,
  input  in_5,
  output out_6,
  output [3:0] out_7
);

  wire adder_1_cout, adder_2_cout, adder_3_cout, adder_4_cout, multiplexer_1_out, multiplexer_2_out,
       multiplexer_3_out, multiplexer_4_out, not_1_out, not_2_out, not_3_out, not_4_out, not_5_out;
  wire [3:0] adder_1_out, and_1_out, multiplexer_5_out, not_6_out, or_1_out, xor_1_out;

  not not_1 (not_1_out, in_4[0]);
  not not_2 (not_2_out, in_4[1]);
  not not_3 (not_3_out, in_4[2]);
  not not_4 (not_4_out, in_4[3]);
  not not_5 (not_5_out, not_5_out);
  assign and_1_out = in_3 & in_4;  // AND_Gate and_1, 4 bits wide
  assign or_1_out = in_3 | in_4;  // OR_Gate or_1, 4 bits wide
  assign xor_1_out = in_3 ^ in_4;  // XOR_Gate xor_1, 4 bits wide
  assign not_6_out = ~in_3;  // NOT_Gate not_6, 4 bits wide
  Multiplexer #(.select(2)) multiplexer_1 (
    .in0(in_4[0]), .in1(not_1_out), .in2(not_5_out), .in3(not_5_out), .out(multiplexer_1_out), .sel(in_1));  // open: en
  Multiplexer #(.select(2)) multiplexer_2 (
    .in0(in_4[1]), .in1(not_2_out), .in2(not_5_out), .in3(not_5_out), .out(multiplexer_2_out), .sel(in_1));  // open: en
  Multiplexer #(.select(2)) multiplexer_3 (
    .in0(in_4[2]), .in1(not_3_out), .in2(not_5_out), .in3(not_5_out), .out(multiplexer_3_out), .sel(in_1));  // open: en
  Multiplexer #(.select(2)) multiplexer_4 (
    .in0(in_4[3]), .in1(not_4_out), .in2(not_5_out), .in3(not_5_out), .out(multiplexer_4_out), .sel(in_1));  // open: en
  Multiplexer #(.select(2), .width(4)) multiplexer_5 (
    .in0(and_1_out), .in1(or_1_out), .in2(xor_1_out), .in3(not_6_out), .out(multiplexer_5_out), .sel(in_1));  // open: en
  Adder #(.width(1)) adder_1 (
    .a(in_3[0]), .b(multiplexer_1_out), .out(adder_1_out[0]), .cin(in_2), .cout(adder_1_cout));
  Adder #(.width(1)) adder_2 (
    .a(in_3[1]), .b(multiplexer_2_out), .out(adder_1_out[1]), .cin(adder_1_cout), .cout(adder_2_cout));
  Adder #(.width(1)) adder_3 (
    .a(in_3[2]), .b(multiplexer_3_out), .out(adder_1_out[2]), .cin(adder_2_cout), .cout(adder_3_cout));
  Adder #(.width(1)) adder_4 (
    .a(in_3[3]), .b(multiplexer_4_out), .out(adder_1_out[3]), .cin(adder_3_cout), .cout(adder_4_cout));
  Multiplexer #(.width(4)) multiplexer_6 (.in0(adder_1_out), .out(out_7), .sel(in_5));  // open: in1, en
  // also tied to GND on the sheet: not_5_out
endmodule

module ALU (
  input  [1:0] S1_S0,
  input  Cin,
  input  [3:0] Register_A,
  input  [3:0] Register_B,
  input  S2,
  input  in_6,
  output out_7,
  output [3:0] out_8
);

  wire adder_1_cout, adder_2_cout, adder_3_cout, adder_4_cout, clock_1_out, multiplexer_1_out,
       multiplexer_2_out, multiplexer_3_out, multiplexer_4_out, not_1_out, not_2_out, not_3_out, not_4_out,
       not_5_out;
  wire [3:0] adder_1_out, and_1_out, multiplexer_5_out, multiplexer_6_out, not_6_out, or_1_out, xor_1_out;

  not not_1 (not_1_out, Register_B[0]);
  not not_2 (not_2_out, Register_B[1]);
  not not_3 (not_3_out, Register_B[2]);
  not not_4 (not_4_out, Register_B[3]);
  not not_5 (not_5_out, not_5_out);
  and and_1 (and_1_out[0], Register_A[0], Register_B[0]);
  and and_2 (and_1_out[1], Register_A[1], Register_B[1]);
  and and_3 (and_1_out[2], Register_A[2], Register_B[2]);
  and and_4 (and_1_out[3], Register_A[3], Register_B[3]);
  or or_1 (or_1_out[0], Register_A[0], Register_B[0]);
  or or_2 (or_1_out[1], Register_A[1], Register_B[1]);
  or or_3 (or_1_out[2], Register_A[2], Register_B[2]);
  or or_4 (or_1_out[3], Register_A[3], Register_B[3]);
  buf xor_1 (xor_1_out[0], Register_A[0]);  // XOR_Gate
  xor xor_2 (xor_1_out[1], Register_A[1], Register_B[1]);
  xor xor_3 (xor_1_out[2], Register_A[2], Register_B[2]);
  xor xor_4 (xor_1_out[3], Register_A[3], Register_B[3]);
  not not_6 (not_6_out[0], Register_A[0]);
  not not_7 (not_6_out[1], Register_A[1]);
  not not_8 (not_6_out[2], Register_A[2]);
  not not_9 (not_6_out[3], Register_A[3]);
  Multiplexer #(.select(2)) multiplexer_1 (
    .in0(Register_B[0]), .in1(not_1_out), .in2(not_5_out), .in3(not_5_out), .out(multiplexer_1_out),
    .sel(S1_S0));  // open: en
  Multiplexer #(.select(2)) multiplexer_2 (
    .in0(Register_B[1]), .in1(not_2_out), .in2(not_5_out), .in3(not_5_out), .out(multiplexer_2_out),
    .sel(S1_S0));  // open: en
  Multiplexer #(.select(2)) multiplexer_3 (
    .in0(Register_B[2]), .in1(not_3_out), .in2(not_5_out), .in3(not_5_out), .out(multiplexer_3_out),
    .sel(S1_S0));  // open: en
  Multiplexer #(.select(2)) multiplexer_4 (
    .in0(Register_B[3]), .in1(not_4_out), .in2(not_5_out), .in3(not_5_out), .out(multiplexer_4_out),
    .sel(S1_S0));  // open: en
  Adder #(.width(1)) adder_1 (
    .a(Register_A[0]), .b(multiplexer_1_out), .out(adder_1_out[0]), .cin(Cin), .cout(adder_1_cout));
  Adder #(.width(1)) adder_2 (
    .a(Register_A[1]), .b(multiplexer_2_out), .out(adder_1_out[1]), .cin(adder_1_cout), .cout(adder_2_cout));
  Adder #(.width(1)) adder_3 (
    .a(Register_A[2]), .b(multiplexer_3_out), .out(adder_1_out[2]), .cin(adder_2_cout), .cout(adder_3_cout));
  Adder #(.width(1)) adder_4 (
    .a(Register_A[3]), .b(multiplexer_4_out), .out(adder_1_out[3]), .cin(adder_3_cout), .cout(adder_4_cout));
  Clock clock_1 (.out(clock_1_out));
  Multiplexer #(.select(2), .width(4)) multiplexer_5 (
    .in0(and_1_out), .in1(or_1_out), .in2(xor_1_out), .out(multiplexer_5_out), .sel(S1_S0));  // open: in3, en
  Multiplexer #(.width(4)) multiplexer_6 (.in0(adder_1_out), .out(multiplexer_6_out), .sel(S2));  // open: in1, en
  Register #(.width(4)) register_1 (.D(multiplexer_6_out), .en(in_6), .Q(out_8), .clk(clock_1_out));  // open: clr
  // also tied to GND on the sheet: not_5_out
endmodule
