// Logisim project alufinal.circ as structural Verilog: 9 circuits, main circuit main
module main (
  input  A0,
  input  A1,
  input  A2,
  input  A3,
  input  B0,
  input  B1,
  input  B2,
  input  B3,
  input  S0,
  input  S1,
  output _0,
  output _1,
  output _2,
  output _3
);

  wire and_1__0, and_1__1, and_1__2, and_1__3, n4_bit_adder_1__0, n4_bit_adder_1__1, n4_bit_adder_1__2,
       n4_bit_adder_1__3, or_1_o0, or_1_o1, or_1_o2, or_1_o3, xor_1_o0, xor_1_o1, xor_1_o2, xor_1_o3;

  _4_bit_adder u_4_bit_adder_1 (
    .A0(A0), .A1(A1), .A2(A2), .A3(A3), .B0(B0), .B1(B1), .B2(B2), .B3(B3), ._0(n4_bit_adder_1__0),
    ._1(n4_bit_adder_1__1), ._2(n4_bit_adder_1__2), ._3(n4_bit_adder_1__3));
  AND and_1 (
    .A0(A0), .A1(A1), .A2(A2), .A3(A3), .B0(B0), .B1(B1), .B2(B2), .B3(B3), ._0(and_1__0), ._1(and_1__1),
    ._2(and_1__2), ._3(and_1__3));
  OR or_1 (
    .A0(A0), .A1(A1), .A2(A2), .A3(A3), .B0(B0), .B1(B1), .B2(B2), .B3(B3), .O0(or_1_o0), .O1(or_1_o1),
    .O2(or_1_o2), .O3(or_1_o3));
  XOR xor_1 (
    .A0(A0), .A1(A1), .A2(A2), .A3(A3), .B0(B0), .B1(B1), .B2(B2), .B3(B3), .O0(xor_1_o0), .O1(xor_1_o1),
    .O2(xor_1_o2), .O3(xor_1_o3));
  _4_1_MUX u_4_1_mux_1 (
    .in_1(n4_bit_adder_1__0), .in_2(n4_bit_adder_1__1), .in_3(n4_bit_adder_1__2), .in_4(n4_bit_adder_1__3),
    .in_5(and_1__0), .in_6(and_1__1), .in_7(and_1__2), .in_8(and_1__3), .in_9(or_1_o0), .in_10(or_1_o1),
    .in_11(or_1_o2), .in_12(or_1_o3), .in_13(xor_1_o0), .in_14(xor_1_o1), .in_15(xor_1_o2), .in_16(xor_1_o3),
    .S1(S0), .S0(S1), .out_19(_0), .out_20(_1), .out_21(_2), .out_22(_3));

  // Notes on the sheet:
  //   ADD
  //   AND
  //   OR
  //   XOR
  //   Selectors
  //   4:1 MUX
endmodule

module _1_bit_adder (
  input  A,
  input  B,
  input  C,
  output S,
  output C_2
);

  wire and_1_out, and_2_out, and_3_out;

  and and_1 (and_1_out, A, B);
  and and_2 (and_2_out, B, C);
  and and_3 (and_3_out, A, C);
  xor xor_1 (S, A, B, C);
  or or_1 (C_2, and_1_out, and_2_out, and_3_out);
endmodule

module _4_bit_adder (
  input  A0,
  input  A1,
  input  A2,
  input  A3,
  input  B0,
  input  B1,
  input  B2,
  input  B3,
  output _0,
  output _1,
  output _2,
  output _3
);

  wire n1_bit_adder_1_c_2, n1_bit_adder_2_c_2, n1_bit_adder_3_c_2, n1_bit_adder_4_c_2;

  _1_bit_adder u_1_bit_adder_1 (.A(A0), .B(B0), .C(1'b0), .S(_0), .C_2(n1_bit_adder_1_c_2));
  _1_bit_adder u_1_bit_adder_2 (.A(A1), .B(B1), .C(n1_bit_adder_1_c_2), .S(_1), .C_2(n1_bit_adder_2_c_2));
  _1_bit_adder u_1_bit_adder_3 (.A(A2), .B(B2), .C(n1_bit_adder_2_c_2), .S(_2), .C_2(n1_bit_adder_3_c_2));
  _1_bit_adder u_1_bit_adder_4 (.A(A3), .B(B3), .C(n1_bit_adder_3_c_2), .S(_3), .C_2(n1_bit_adder_4_c_2));

  // Notes on the sheet:
  //   C
  //   C
endmodule

module AND (
  input  A0,
  input  A1,
  input  A2,
  input  A3,
  input  B0,
  input  B1,
  input  B2,
  input  B3,
  output _0,
  output _1,
  output _2,
  output _3
);

  and and_1 (_0, A0, B0);
  and and_2 (_1, A1, B1);
  and and_3 (_2, A2, B2);
  and and_4 (_3, A3, B3);
endmodule

module OR (
  input  A0,
  input  A1,
  input  A2,
  input  A3,
  input  B0,
  input  B1,
  input  B2,
  input  B3,
  output O0,
  output O1,
  output O2,
  output O3
);

  or or_1 (O0, A0, B0);
  or or_2 (O1, A1, B1);
  or or_3 (O2, A2, B2);
  or or_4 (O3, A3, B3);
endmodule

module XOR (
  input  A0,
  input  A1,
  input  A2,
  input  A3,
  input  B0,
  input  B1,
  input  B2,
  input  B3,
  output O0,
  output O1,
  output O2,
  output O3
);

  xor xor_1 (O0, A0, B0);
  xor xor_2 (O1, A1, B1);
  xor xor_3 (O2, A2, B2);
  xor xor_4 (O3, A3, B3);
endmodule

module _4_1_MUX (
  input  in_1,
  input  in_2,
  input  in_3,
  input  in_4,
  input  in_5,
  input  in_6,
  input  in_7,
  input  in_8,
  input  in_9,
  input  in_10,
  input  in_11,
  input  in_12,
  input  in_13,
  input  in_14,
  input  in_15,
  input  in_16,
  input  S1,
  input  S0,
  output out_19,
  output out_20,
  output out_21,
  output out_22
);

  mux mux_1 (.A(in_1), .B(in_5), .C(in_9), .D(in_13), .S1(S1), .S0(S0), .out(out_19));
  mux mux_2 (.A(in_2), .B(in_6), .C(in_10), .D(in_14), .S1(S1), .S0(S0), .out(out_20));
  mux mux_3 (.A(in_3), .B(in_7), .C(in_11), .D(in_15), .S1(S1), .S0(S0), .out(out_21));
  mux mux_4 (.A(in_4), .B(in_8), .C(in_12), .D(in_16), .S1(S1), .S0(S0), .out(out_22));

  // Notes on the sheet:
  //   mux
endmodule

module mux (
  input  A,
  input  B,
  input  C,
  input  D,
  input  S1,
  input  S0,
  output out
);

  wire multiplexer_1_out, multiplexer_2_out;

  Multiplexer #(.enable("false")) multiplexer_1 (.in0(A), .in1(B), .out(multiplexer_1_out), .sel(S1));
  Multiplexer #(.enable("false")) multiplexer_2 (.in0(C), .in1(D), .out(multiplexer_2_out), .sel(S1));
  Multiplexer #(.enable("false")) multiplexer_3 (.in0(multiplexer_1_out), .in1(multiplexer_2_out), .out(out), .sel(S0));
endmodule

module _2_1_Mux (
  input  A,
  input  B,
  input  S,
  output out_4
);

  wire and_1_out, and_2_out, not_1_out;

  not not_1 (not_1_out, S);
  and and_1 (and_1_out, A, not_1_out);
  and and_2 (and_2_out, B, S);
  or or_1 (out_4, and_1_out, and_2_out);
endmodule
