// Logisim project final.circ as structural Verilog: 16 circuits, main circuit main
module main (
);

  wire and_1_out, clock_1_out, register_file_1_out_11, selector_1_o0, selector_1_o1, selector_1_o2,
       selector_1_o3;
  wire [3:0] alu_1_o0, rom_1_data, rom_1_data_2;
  wire [6:0] register_file_1_out_12;
  wire [7:0] counter_1_q, rom_2_data;

  Clock clock_1 (.out(clock_1_out));
  Counter counter_1 (.Q(counter_1_q), .clk(clock_1_out), .clr(and_1_out));  // open: load, D, count, carry
  ROM rom_1 (.addr(counter_1_q), .data({rom_1_data_2, rom_1_data}));  // open: sel
  ROM #(.addrWidth(4)) rom_2 (.addr(rom_1_data_2), .data(rom_2_data));  // open: sel
  Selector selector_1 (
    .A0(rom_1_data[0]), .A1(rom_1_data[1]), .A2(rom_1_data[2]), .A3(rom_1_data[3]), .B0(alu_1_o0[0]),
    .B1(alu_1_o0[1]), .B2(alu_1_o0[2]), .B3(alu_1_o0[3]), .Z0(rom_2_data[3]), .O0(selector_1_o0),
    .O1(selector_1_o1), .O2(selector_1_o2), .O3(selector_1_o3));
  and and_1 (and_1_out, rom_2_data[6], rom_2_data[7]);
  register_file register_file_1 (
    .A0(selector_1_o0), .A1(selector_1_o1), .A2(selector_1_o2), .A3(selector_1_o3), .WE(rom_2_data[0]),
    .S0(rom_2_data[1]), .in_6(clock_1_out), .out_8(register_file_1_out_12[4]),
    .out_9(register_file_1_out_12[5]), .out_10(register_file_1_out_12[6]), .out_11(register_file_1_out_11),
    .out_12(register_file_1_out_12[0]), .out_13(register_file_1_out_12[1]),
    .out_14(register_file_1_out_12[2]), .out_15(register_file_1_out_12[3]));
  ALU alu_1 (
    .D0(rom_2_data[7]), .A0(register_file_1_out_12[4]), .A1(register_file_1_out_12[5]),
    .A2(register_file_1_out_12[6]), .A3(register_file_1_out_11), .B0(register_file_1_out_12[0]),
    .B1(register_file_1_out_12[1]), .B2(register_file_1_out_12[2]), .B3(register_file_1_out_12[3]),
    .S0(rom_2_data[5]), .S1(rom_2_data[6]), .Clock(clock_1_out), .WE(rom_2_data[4]), .O0(alu_1_o0[0]),
    .O1(alu_1_o0[1]), .O2(alu_1_o0[2]), .O3(alu_1_o0[3]));
  TTY tty_1 (.data(register_file_1_out_12), .clk(clock_1_out), .we(rom_2_data[2]), .clr(and_1_out));

  // Notes on the sheet:
  //   Binary Counter
  //   Clock
  //   Program PROM
  //   Instruction Decoder
  //   contents of rom_1 (hex, n*v repeats v):
  //   23 13 30 1b 22 30 23 14 30 1d 23 30 23 14 60 40 23 30 1d 20 30 13 23 30 1a 22 30 13 23 30 1d 23 30
  //   13 23 60 40 60 40 30 1d 20 30 14 23 30 1d 22 30 13 23 30 1d 23 30 13 2f 90 21 40 60 40 24 60 40 23
  //   30 1d 20 30 14 23
  //   contents of rom_2 (hex, n*v repeats v):
  //   0 3 1 4 b a 10 30 50 70 90 c0
  //   Register File
endmodule

module _1_bit_adder (
  input  A1,
  input  A2,
  input  A3,
  output S,
  output C
);

  wire and_1_out, and_2_out, and_3_out;

  and and_1 (and_1_out, A1, A2);
  and and_2 (and_2_out, A2, A3);
  and and_3 (and_3_out, A1, A3);
  xor xor_1 (S, A1, A2, A3);
  or or_1 (C, and_1_out, and_2_out, and_3_out);
endmodule

module _4_bit_adder (
  input  A0,
  input  A1,
  input  A2,
  input  A3,
  input  B0,
  input  B1,
  input  B2,
  input  B3,
  output _0,
  output _1,
  output _2,
  output _3
);

  wire _4_Bit_adder_c, n1_bit_adder_1_c, n1_bit_adder_2_c, n1_bit_adder_3_c;

  _1_bit_adder _4_Bit_adder (.A1(A0), .A2(B0), .A3(1'b0), .S(_0), .C(_4_Bit_adder_c));
  _1_bit_adder u_1_bit_adder_1 (.A1(A1), .A2(B1), .A3(_4_Bit_adder_c), .S(_1), .C(n1_bit_adder_1_c));
  _1_bit_adder u_1_bit_adder_2 (.A1(A2), .A2(B2), .A3(n1_bit_adder_1_c), .S(_2), .C(n1_bit_adder_2_c));
  _1_bit_adder u_1_bit_adder_3 (.A1(A3), .A2(B3), .A3(n1_bit_adder_2_c), .S(_3), .C(n1_bit_adder_3_c));

  // Notes on the sheet:
  //   C
  //   C
endmodule

module AND (
  input  A0,
  input  A1,
  input  A2,
  input  A3,
  input  B0,
  input  B1,
  input  B2,
  input  B3,
  output _0,
  output _1,
  output _2,
  output _3
);

  and and_1 (_0, A0, B0);
  and and_2 (_1, A1, B1);
  and and_3 (_2, A2, B2);
  and and_4 (_3, A3, B3);
endmodule

module OR (
  input  A0,
  input  A1,
  input  A2,
  input  A3,
  input  B0,
  input  B1,
  input  B2,
  input  B3,
  output O0,
  output O1,
  output O2,
  output O3
);

  or or_1 (O0, A0, B0);
  or or_2 (O1, A1, B1);
  or or_3 (O2, A2, B2);
  or or_4 (O3, A3, B3);
endmodule

module XOR (
  input  A0,
  input  A1,
  input  A2,
  input  A3,
  input  B0,
  input  B1,
  input  B2,
  input  B3,
  output O0,
  output O1,
  output O2,
  output O3
);

  xor xor_1 (O0, A0, B0);
  xor xor_2 (O1, A1, B1);
  xor xor_3 (O2, A2, B2);
  xor xor_4 (O3, A3, B3);
endmodule

module _4X4_1_MUX (
  input  in_1,
  input  in_2,
  input  in_3,
  input  in_4,
  input  in_5,
  input  in_6,
  input  in_7,
  input  in_8,
  input  in_9,
  input  in_10,
  input  in_11,
  input  in_12,
  input  in_13,
  input  in_14,
  input  in_15,
  input  in_16,
  input  S1,
  input  S0,
  output out_19,
  output out_20,
  output out_21,
  output out_22
);

  mux mux_1 (.A(in_1), .B(in_5), .C(in_9), .D(in_13), .S1(S1), .S0(S0), .out(out_19));
  mux mux_2 (.A(in_2), .B(in_6), .C(in_10), .D(in_14), .S1(S1), .S0(S0), .out(out_20));
  mux mux_3 (.A(in_3), .B(in_7), .C(in_11), .D(in_15), .S1(S1), .S0(S0), .out(out_21));
  mux mux_4 (.A(in_4), .B(in_8), .C(in_12), .D(in_16), .S1(S1), .S0(S0), .out(out_22));
endmodule

// 4:1 MUX
module mux (
  input  A,
  input  B,
  input  C,
  input  D,
  input  S1,
  input  S0,
  output out
);

  wire multiplexer_1_out, multiplexer_2_out;

  Multiplexer #(.enable("false")) multiplexer_1 (.in0(A), .in1(B), .out(multiplexer_1_out), .sel(S1));
  Multiplexer #(.enable("false")) multiplexer_2 (.in0(C), .in1(D), .out(multiplexer_2_out), .sel(S1));
  Multiplexer #(.enable("false")) multiplexer_3 (.in0(multiplexer_1_out), .in1(multiplexer_2_out), .out(out), .sel(S0));
endmodule

module _2_1_Mux (
  input  A,
  input  B,
  input  S,
  output out_4
);

  wire and_1_out, and_2_out, not_1_out;

  not not_1 (not_1_out, S);
  and and_1 (and_1_out, A, not_1_out);
  and and_2 (and_2_out, B, S);
  or or_1 (out_4, and_1_out, and_2_out);
endmodule

module _3_8_line_decoder (
  input  in_1,
  input  in_2,
  input  in_3,
  input  clock,
  output out_5,
  output out_6,
  output out_7,
  output out_8,
  output \output ,
  output out_10,
  output out_11,
  output out_12
);

  wire not_1_out, not_2_out, not_3_out;

  not not_1 (not_1_out, in_1);
  not not_2 (not_2_out, in_2);
  not not_3 (not_3_out, in_3);
  and and_1 (out_5, not_1_out, not_2_out, not_3_out, clock);
  and and_2 (out_6, in_1, not_2_out, not_3_out, clock);
  and and_3 (out_7, not_1_out, in_2, not_3_out, clock);
  and and_4 (out_8, in_1, in_2, not_3_out, clock);
  and and_5 (\output , not_1_out, not_2_out, in_3, clock);
  and and_6 (out_10, in_1, not_2_out, in_3, clock);
  and and_7 (out_11, not_1_out, in_2, in_3, clock);
  and and_8 (out_12, in_1, in_2, in_3, clock);

  // Notes on the sheet:
  //   inputs
endmodule

// 1 Bit
module _1_bit_register (
  input  Clock,
  input  Input,
  input  Load,
  output Out
);

  wire n2_1_mux_1_out_4;

  _2_1_Mux u_2_1_mux_1 (.A(Out), .B(Input), .S(Load), .out_4(n2_1_mux_1_out_4));
  D_Flip_Flop d_ff_1 (.clk(Clock), .D(n2_1_mux_1_out_4), .Q(Out));  // open: Qn, preset, en, reset
endmodule

// 4-BIT Reg
module _4_bit_register (
  input  A0,
  input  A1,
  input  A2,
  input  A3,
  input  clock,
  input  Load,
  output O1,
  output O2,
  output O3,
  output O4
);

  _1_bit_register u_1_bit_register_1 (.Input(A0), .Clock(clock), .Load(Load), .Out(O1));
  _1_bit_register u_1_bit_register_2 (.Input(A2), .Clock(clock), .Load(Load), .Out(O3));
  _1_bit_register u_1_bit_register_3 (.Input(A3), .Clock(clock), .Load(Load), .Out(O4));
  _1_bit_register u_1_bit_register_4 (.Input(A1), .Clock(clock), .Load(Load), .Out(O2));
endmodule

// Register File
module register_file (
  input  A0,
  input  A1,
  input  A2,
  input  A3,
  input  WE,
  input  in_6,
  input  S0,
  output out_8,
  output out_9,
  output out_10,
  output out_11,
  output out_12,
  output out_13,
  output out_14,
  output out_15
);

  wire and_1_out, and_2_out, not_1_out;

  not not_1 (not_1_out, S0);
  and and_1 (and_1_out, WE, not_1_out);
  and and_2 (and_2_out, WE, S0);
  _4_bit_register u_4_bit_register_1 (
    .A0(A0), .A1(A1), .A2(A2), .A3(A3), .clock(in_6), .Load(and_1_out), .O1(out_8), .O2(out_9), .O3(out_10),
    .O4(out_11));
  _4_bit_register u_4_bit_register_2 (
    .A0(A0), .A1(A1), .A2(A2), .A3(A3), .clock(in_6), .Load(and_2_out), .O1(out_12), .O2(out_13),
    .O3(out_14), .O4(out_15));

  // Notes on the sheet:
  //   Clock
endmodule

module ALU (
  input  D0,
  input  A0,
  input  A1,
  input  A2,
  input  A3,
  input  B0,
  input  B1,
  input  B2,
  input  B3,
  input  S0,
  input  S1,
  input  Clock,
  input  WE,
  output O0,
  output O1,
  output O2,
  output O3
);

  wire adder_subtractor_1_out_0, adder_subtractor_1_out_1, adder_subtractor_1_out_2,
       adder_subtractor_1_out_3, and_1__0, and_1__1, and_1__2, and_1__3, n4x4_1_mux_1_out_19,
       n4x4_1_mux_1_out_20, n4x4_1_mux_1_out_21, n4x4_1_mux_1_out_22, or_1_o0, or_1_o1, or_1_o2, or_1_o3,
       xor_1_o0, xor_1_o1, xor_1_o2, xor_1_o3;

  Adder_subtractor adder_subtractor_1 (
    .A0(A0), .A1(A1), .A2(A2), .A3(A3), .B0(B0), .B1(B1), .B2(B2), .B3(B3), .Z0(D0),
    .OUT_0(adder_subtractor_1_out_0), .OUT_1(adder_subtractor_1_out_1), .OUT_2(adder_subtractor_1_out_2),
    .OUT_3(adder_subtractor_1_out_3));
  OR or_1 (
    .A0(A0), .A1(A1), .A2(A2), .A3(A3), .B0(B0), .B1(B1), .B2(B2), .B3(B3), .O0(or_1_o0), .O1(or_1_o1),
    .O2(or_1_o2), .O3(or_1_o3));
  AND and_1 (
    .A0(A0), .A1(A1), .A2(A2), .A3(A3), .B0(B0), .B1(B1), .B2(B2), .B3(B3), ._0(and_1__0), ._1(and_1__1),
    ._2(and_1__2), ._3(and_1__3));
  XOR xor_1 (
    .A0(A0), .A1(A1), .A2(A2), .A3(A3), .B0(B0), .B1(B1), .B2(B2), .B3(B3), .O0(xor_1_o0), .O1(xor_1_o1),
    .O2(xor_1_o2), .O3(xor_1_o3));
  _4X4_1_MUX u_4x4_1_mux_1 (
    .in_1(adder_subtractor_1_out_0), .in_2(adder_subtractor_1_out_1), .in_3(adder_subtractor_1_out_2),
    .in_4(adder_subtractor_1_out_3), .in_5(or_1_o0), .in_6(or_1_o1), .in_7(or_1_o2), .in_8(or_1_o3),
    .in_9(and_1__0), .in_10(and_1__1), .in_11(and_1__2), .in_12(and_1__3), .in_13(xor_1_o0),
    .in_14(xor_1_o1), .in_15(xor_1_o2), .in_16(xor_1_o3), .S1(S0), .S0(S1), .out_19(n4x4_1_mux_1_out_19),
    .out_20(n4x4_1_mux_1_out_20), .out_21(n4x4_1_mux_1_out_21), .out_22(n4x4_1_mux_1_out_22));
  _4_bit_register u_4_bit_register_1 (
    .A0(n4x4_1_mux_1_out_19), .A1(n4x4_1_mux_1_out_20), .A2(n4x4_1_mux_1_out_21), .A3(n4x4_1_mux_1_out_22),
    .clock(Clock), .Load(WE), .O1(O0), .O2(O1), .O3(O2), .O4(O3));

  // Notes on the sheet:
  //   Inputs
  //   Selectors
  //   Accumulator
  //   Register Controls
  //   Outputs
endmodule

// SELECTOR
module Selector (
  input  A0,
  input  A1,
  input  A2,
  input  A3,
  input  B0,
  input  B1,
  input  B2,
  input  B3,
  input  Z0,
  output O0,
  output O1,
  output O2,
  output O3
);

  wire and_1_out, and_2_out, and_3_out, and_4_out, and_5_out, and_6_out, and_7_out, and_8_out, not_1_out;

  not not_1 (not_1_out, Z0);
  and and_1 (and_1_out, A0, not_1_out);
  and and_2 (and_2_out, A1, not_1_out);
  and and_3 (and_3_out, A2, not_1_out);
  and and_4 (and_4_out, A3, not_1_out);
  and and_5 (and_5_out, B0, Z0);
  and and_6 (and_6_out, B1, Z0);
  and and_7 (and_7_out, B2, Z0);
  and and_8 (and_8_out, B3, Z0);
  or or_1 (O0, and_1_out, and_5_out);
  or or_2 (O1, and_2_out, and_6_out);
  or or_3 (O2, and_3_out, and_7_out);
  or or_4 (O3, and_4_out, and_8_out);
endmodule

// ADD/SUB
module Adder_subtractor (
  input  Z0,
  input  A0,
  input  A1,
  input  A2,
  input  A3,
  input  B0,
  input  B1,
  input  B2,
  input  B3,
  output OUT_0,
  output OUT_1,
  output OUT_2,
  output OUT_3
);

  wire _1_Bit_Adder_2_c, _1_Bit_Adder_3_c, _1_Bit_Adder_4_c, _1_Bit_Adder_c, xor_1_out, xor_2_out, xor_3_out,
       xor_4_out;

  xor xor_1 (xor_1_out, Z0, B0);
  xor xor_2 (xor_2_out, Z0, B1);
  xor xor_3 (xor_3_out, Z0, B2);
  xor xor_4 (xor_4_out, Z0, B3);
  _1_bit_adder _1_Bit_Adder (.A1(A0), .A2(xor_1_out), .A3(Z0), .S(OUT_0), .C(_1_Bit_Adder_c));
  _1_bit_adder _1_Bit_Adder_2 (.A1(A1), .A2(xor_2_out), .A3(_1_Bit_Adder_c), .S(OUT_1), .C(_1_Bit_Adder_2_c));
  _1_bit_adder _1_Bit_Adder_3 (.A1(A2), .A2(xor_3_out), .A3(_1_Bit_Adder_2_c), .S(OUT_2), .C(_1_Bit_Adder_3_c));
  _1_bit_adder _1_Bit_Adder_4 (.A1(A3), .A2(xor_4_out), .A3(_1_Bit_Adder_3_c), .S(OUT_3), .C(_1_Bit_Adder_4_c));
  // also tied to GND on the sheet: _1_Bit_Adder_4_c

  // Notes on the sheet:
  //   C
endmodule
