// Logisim project mp.circ as structural Verilog: 12 circuits, main circuit main
module main (
  input  A0,
  input  A1,
  input  A2,
  input  A3,
  input  B0,
  input  B1,
  input  B2,
  input  B3,
  input  In_0,
  input  S0,
  input  S1,
  input  In_1,
  input  In_2,
  input  In_3,
  input  Clock_input,
  input  A0_2,
  input  A1_2,
  input  A2_2,
  input  WE,
  output _0,
  output _1,
  output _2,
  output _3,
  output OUT_0,
  output OUT_1,
  output OUT_2,
  output OUT_3
);

  wire and_1__0, and_1__1, and_1__2, and_1__3, n3_8_line_decoder_1_out_5, n3_8_line_decoder_1_out_6,
       n3_8_line_decoder_1_out_7, n3_8_line_decoder_1_out_8, n3_8_line_decoder_1_out_10,
       n3_8_line_decoder_1_out_11, n3_8_line_decoder_1_out_12, n3_8_line_decoder_1_output, n4_bit_adder_1__0,
       n4_bit_adder_1__1, n4_bit_adder_1__2, n4_bit_adder_1__3, or_1_o0, or_1_o1, or_1_o2, or_1_o3, xor_1_o0,
       xor_1_o1, xor_1_o2, xor_1_o3;
  wire [3:0] n4_bit_register_1_out_7, n4_bit_register_2_out_7, n4_bit_register_3_out_7,
       n4_bit_register_4_out_7, n4_bit_register_5_out_7, n4_bit_register_6_out_7, n4_bit_register_7_out_7,
       n4_bit_register_8_out_7;

  _4_bit_adder u_4_bit_adder_1 (
    .A0(A0), .A1(A1), .A2(A2), .A3(A3), .B0(B0), .B1(B1), .B2(B2), .B3(B3), ._0(n4_bit_adder_1__0),
    ._1(n4_bit_adder_1__1), ._2(n4_bit_adder_1__2), ._3(n4_bit_adder_1__3));
  AND and_1 (
    .A0(A0), .A1(A1), .A2(A2), .A3(A3), .B0(B0), .B1(B1), .B2(B2), .B3(B3), ._0(and_1__0), ._1(and_1__1),
    ._2(and_1__2), ._3(and_1__3));
  OR or_1 (
    .A0(A0), .A1(A1), .A2(A2), .A3(A3), .B0(B0), .B1(B1), .B2(B2), .B3(B3), .O0(or_1_o0), .O1(or_1_o1),
    .O2(or_1_o2), .O3(or_1_o3));
  XOR xor_1 (
    .A0(A0), .A1(A1), .A2(A2), .A3(A3), .B0(B0), .B1(B1), .B2(B2), .B3(B3), .O0(xor_1_o0), .O1(xor_1_o1),
    .O2(xor_1_o2), .O3(xor_1_o3));
  _4_1_MUX u_4_1_mux_1 (
    .in_1(n4_bit_adder_1__0), .in_2(n4_bit_adder_1__1), .in_3(n4_bit_adder_1__2), .in_4(n4_bit_adder_1__3),
    .in_5(and_1__0), .in_6(and_1__1), .in_7(and_1__2), .in_8(and_1__3), .in_9(or_1_o0), .in_10(or_1_o1),
    .in_11(or_1_o2), .in_12(or_1_o3), .in_13(xor_1_o0), .in_14(xor_1_o1), .in_15(xor_1_o2), .in_16(xor_1_o3),
    .S1(S0), .S0(S1), .out_19(_0), .out_20(_1), .out_21(_2), .out_22(_3));
  _3_8_line_decoder u_3_8_line_decoder_1 (
    .in_1(A0_2), .in_2(A1_2), .in_3(A2_2), .clock(WE), .out_5(n3_8_line_decoder_1_out_5),
    .out_6(n3_8_line_decoder_1_out_6), .out_7(n3_8_line_decoder_1_out_7), .out_8(n3_8_line_decoder_1_out_8),
    .\output (n3_8_line_decoder_1_output), .out_10(n3_8_line_decoder_1_out_10),
    .out_11(n3_8_line_decoder_1_out_11), .out_12(n3_8_line_decoder_1_out_12));
  _4_bit_register u_4_bit_register_1 (
    .in_1(In_0), .in_2(In_1), .inputs(In_2), .in_4(In_3), .clock(Clock_input),
    .in_6(n3_8_line_decoder_1_out_5), .out_7(n4_bit_register_1_out_7[0]),
    .Outputs(n4_bit_register_1_out_7[1]), .out_9(n4_bit_register_1_out_7[2]),
    .out_10(n4_bit_register_1_out_7[3]));
  _4_bit_register u_4_bit_register_2 (
    .in_1(In_0), .in_2(In_1), .inputs(In_2), .in_4(In_3), .clock(Clock_input),
    .in_6(n3_8_line_decoder_1_out_7), .out_7(n4_bit_register_2_out_7[0]),
    .Outputs(n4_bit_register_2_out_7[1]), .out_9(n4_bit_register_2_out_7[2]),
    .out_10(n4_bit_register_2_out_7[3]));
  _4_bit_register u_4_bit_register_3 (
    .in_1(In_0), .in_2(In_1), .inputs(In_2), .in_4(In_3), .clock(Clock_input),
    .in_6(n3_8_line_decoder_1_output), .out_7(n4_bit_register_3_out_7[0]),
    .Outputs(n4_bit_register_3_out_7[1]), .out_9(n4_bit_register_3_out_7[2]),
    .out_10(n4_bit_register_3_out_7[3]));
  _4_bit_register u_4_bit_register_4 (
    .in_1(In_0), .in_2(In_1), .inputs(In_2), .in_4(In_3), .clock(Clock_input),
    .in_6(n3_8_line_decoder_1_out_11), .out_7(n4_bit_register_4_out_7[0]),
    .Outputs(n4_bit_register_4_out_7[1]), .out_9(n4_bit_register_4_out_7[2]),
    .out_10(n4_bit_register_4_out_7[3]));
  _4_bit_register u_4_bit_register_5 (
    .in_1(In_0), .in_2(In_1), .inputs(In_2), .in_4(In_3), .clock(Clock_input),
    .in_6(n3_8_line_decoder_1_out_6), .out_7(n4_bit_register_5_out_7[0]),
    .Outputs(n4_bit_register_5_out_7[1]), .out_9(n4_bit_register_5_out_7[2]),
    .out_10(n4_bit_register_5_out_7[3]));
  _4_bit_register u_4_bit_register_6 (
    .in_1(In_0), .in_2(In_1), .inputs(In_2), .in_4(In_3), .clock(Clock_input),
    .in_6(n3_8_line_decoder_1_out_8), .out_7(n4_bit_register_6_out_7[0]),
    .Outputs(n4_bit_register_6_out_7[1]), .out_9(n4_bit_register_6_out_7[2]),
    .out_10(n4_bit_register_6_out_7[3]));
  _4_bit_register u_4_bit_register_7 (
    .in_1(In_0), .in_2(In_1), .inputs(In_2), .in_4(In_3), .clock(Clock_input),
    .in_6(n3_8_line_decoder_1_out_10), .out_7(n4_bit_register_7_out_7[0]),
    .Outputs(n4_bit_register_7_out_7[1]), .out_9(n4_bit_register_7_out_7[2]),
    .out_10(n4_bit_register_7_out_7[3]));
  _4_bit_register u_4_bit_register_8 (
    .in_1(In_0), .in_2(In_1), .inputs(In_2), .in_4(In_3), .clock(Clock_input),
    .in_6(n3_8_line_decoder_1_out_12), .out_7(n4_bit_register_8_out_7[0]),
    .Outputs(n4_bit_register_8_out_7[1]), .out_9(n4_bit_register_8_out_7[2]),
    .out_10(n4_bit_register_8_out_7[3]));
  Multiplexer #(.select(3), .width(4), .enable("false")) multiplexer_1 (
    .in0(n4_bit_register_1_out_7), .in1(n4_bit_register_5_out_7), .in2(n4_bit_register_2_out_7),
    .in3(n4_bit_register_6_out_7), .in4(n4_bit_register_3_out_7), .in5(n4_bit_register_7_out_7),
    .in6(n4_bit_register_4_out_7), .in7(n4_bit_register_8_out_7), .out({OUT_3, OUT_2, OUT_1, OUT_0}),
    .sel({A2_2, A1_2, A0_2}));

  // Notes on the sheet:
  //   ADD
  //   AND
  //   OR
  //   XOR
  //   Selectors
  //   4:1 MUX
  //   3:8 Decoder
  //   4 bit register
  //   4 bit register
  //   4 bit register
  //   4 bit register
  //   4 bit register
  //   4 bit register
  //   4 bit register
endmodule

module _1_bit_adder (
  input  A,
  input  B,
  input  C,
  output S,
  output C_2
);

  wire and_1_out, and_2_out, and_3_out;

  and and_1 (and_1_out, A, B);
  and and_2 (and_2_out, B, C);
  and and_3 (and_3_out, A, C);
  xor xor_1 (S, A, B, C);
  or or_1 (C_2, and_1_out, and_2_out, and_3_out);
endmodule

module _4_bit_adder (
  input  A0,
  input  A1,
  input  A2,
  input  A3,
  input  B0,
  input  B1,
  input  B2,
  input  B3,
  output _0,
  output _1,
  output _2,
  output _3
);

  wire n1_bit_adder_1_c_2, n1_bit_adder_2_c_2, n1_bit_adder_3_c_2, n1_bit_adder_4_c_2;

  _1_bit_adder u_1_bit_adder_1 (.A(A0), .B(B0), .C(1'b0), .S(_0), .C_2(n1_bit_adder_1_c_2));
  _1_bit_adder u_1_bit_adder_2 (.A(A1), .B(B1), .C(n1_bit_adder_1_c_2), .S(_1), .C_2(n1_bit_adder_2_c_2));
  _1_bit_adder u_1_bit_adder_3 (.A(A2), .B(B2), .C(n1_bit_adder_2_c_2), .S(_2), .C_2(n1_bit_adder_3_c_2));
  _1_bit_adder u_1_bit_adder_4 (.A(A3), .B(B3), .C(n1_bit_adder_3_c_2), .S(_3), .C_2(n1_bit_adder_4_c_2));

  // Notes on the sheet:
  //   C
  //   C
endmodule

module AND (
  input  A0,
  input  A1,
  input  A2,
  input  A3,
  input  B0,
  input  B1,
  input  B2,
  input  B3,
  output _0,
  output _1,
  output _2,
  output _3
);

  and and_1 (_0, A0, B0);
  and and_2 (_1, A1, B1);
  and and_3 (_2, A2, B2);
  and and_4 (_3, A3, B3);
endmodule

module OR (
  input  A0,
  input  A1,
  input  A2,
  input  A3,
  input  B0,
  input  B1,
  input  B2,
  input  B3,
  output O0,
  output O1,
  output O2,
  output O3
);

  or or_1 (O0, A0, B0);
  or or_2 (O1, A1, B1);
  or or_3 (O2, A2, B2);
  or or_4 (O3, A3, B3);
endmodule

module XOR (
  input  A0,
  input  A1,
  input  A2,
  input  A3,
  input  B0,
  input  B1,
  input  B2,
  input  B3,
  output O0,
  output O1,
  output O2,
  output O3
);

  xor xor_1 (O0, A0, B0);
  xor xor_2 (O1, A1, B1);
  xor xor_3 (O2, A2, B2);
  xor xor_4 (O3, A3, B3);
endmodule

module _4_1_MUX (
  input  in_1,
  input  in_2,
  input  in_3,
  input  in_4,
  input  in_5,
  input  in_6,
  input  in_7,
  input  in_8,
  input  in_9,
  input  in_10,
  input  in_11,
  input  in_12,
  input  in_13,
  input  in_14,
  input  in_15,
  input  in_16,
  input  S1,
  input  S0,
  output out_19,
  output out_20,
  output out_21,
  output out_22
);

  mux mux_1 (.A(in_1), .B(in_5), .C(in_9), .D(in_13), .S1(S1), .S0(S0), .out(out_19));
  mux mux_2 (.A(in_2), .B(in_6), .C(in_10), .D(in_14), .S1(S1), .S0(S0), .out(out_20));
  mux mux_3 (.A(in_3), .B(in_7), .C(in_11), .D(in_15), .S1(S1), .S0(S0), .out(out_21));
  mux mux_4 (.A(in_4), .B(in_8), .C(in_12), .D(in_16), .S1(S1), .S0(S0), .out(out_22));

  // Notes on the sheet:
  //   mux
endmodule

module mux (
  input  A,
  input  B,
  input  C,
  input  D,
  input  S1,
  input  S0,
  output out
);

  wire multiplexer_1_out, multiplexer_2_out;

  Multiplexer #(.enable("false")) multiplexer_1 (.in0(A), .in1(B), .out(multiplexer_1_out), .sel(S1));
  Multiplexer #(.enable("false")) multiplexer_2 (.in0(C), .in1(D), .out(multiplexer_2_out), .sel(S1));
  Multiplexer #(.enable("false")) multiplexer_3 (.in0(multiplexer_1_out), .in1(multiplexer_2_out), .out(out), .sel(S0));
endmodule

module _2_1_Mux (
  input  A,
  input  B,
  input  S,
  output out_4
);

  wire and_1_out, and_2_out, not_1_out;

  not not_1 (not_1_out, S);
  and and_1 (and_1_out, A, not_1_out);
  and and_2 (and_2_out, B, S);
  or or_1 (out_4, and_1_out, and_2_out);
endmodule

module _3_8_line_decoder (
  input  in_1,
  input  in_2,
  input  in_3,
  input  clock,
  output out_5,
  output out_6,
  output out_7,
  output out_8,
  output \output ,
  output out_10,
  output out_11,
  output out_12
);

  wire not_1_out, not_2_out, not_3_out;

  not not_1 (not_1_out, in_1);
  not not_2 (not_2_out, in_2);
  not not_3 (not_3_out, in_3);
  and and_1 (out_5, not_1_out, not_2_out, not_3_out, clock);
  and and_2 (out_6, in_1, not_2_out, not_3_out, clock);
  and and_3 (out_7, not_1_out, in_2, not_3_out, clock);
  and and_4 (out_8, in_1, in_2, not_3_out, clock);
  and and_5 (\output , not_1_out, not_2_out, in_3, clock);
  and and_6 (out_10, in_1, not_2_out, in_3, clock);
  and and_7 (out_11, not_1_out, in_2, in_3, clock);
  and and_8 (out_12, in_1, in_2, in_3, clock);

  // Notes on the sheet:
  //   inputs
endmodule

module _1_bit_register (
  input  clock,
  input  in_2,
  input  in_3,
  output \output 
);

  wire multiplexer_1_out;

  Multiplexer #(.enable("false")) multiplexer_1 (.in0(\output ), .in1(in_2), .out(multiplexer_1_out), .sel(in_3));
  D_Flip_Flop d_ff_1 (.clk(clock), .D(multiplexer_1_out), .Q(\output ));  // open: Qn, preset, en, reset
endmodule

module _4_bit_register (
  input  in_1,
  input  in_2,
  input  inputs,
  input  in_4,
  input  clock,
  input  in_6,
  output out_7,
  output Outputs,
  output out_9,
  output out_10
);

  _1_bit_register u_1_bit_register_1 (.clock(clock), .in_2(in_1), .in_3(in_6), .\output (out_7));
  _1_bit_register u_1_bit_register_2 (.clock(clock), .in_2(in_2), .in_3(in_6), .\output (Outputs));
  _1_bit_register u_1_bit_register_3 (.clock(clock), .in_2(inputs), .in_3(in_6), .\output (out_9));
  _1_bit_register u_1_bit_register_4 (.clock(clock), .in_2(in_4), .in_3(in_6), .\output (out_10));

  // Notes on the sheet:
  //   4, 1 bit registers
endmodule
